# Fritzing sketch itabag schematic (saved by Fritzing 0.9.2b)

parts:
  Part1 = Adafruit Circuit Playground Dev Edition [part_number="Adafruit #3000"]
  NEOPIXEL1 = Neopixel Strip -- White (60/m)
  R1 = Resistor [tolerance=±5% resistance=470 package=THT]

nets:
  N1: Part1.D6, R1.Pin_0
  GND: Part1.GND, NEOPIXEL1.GND
  N2: Part1.VBAT, NEOPIXEL1.+5V
  N3: NEOPIXEL1.DI, R1.Pin_1

custom parts:
  Adafruit Circuit Playground Dev Edition: Would you like to learn electronics, with an all-in-one board that has sensors and LEDs built in? Circuit Playground is here - and it's the best way to practice programming on real hardware with no soldering or sewing required! Circuit Playground features an ATmega32u4 processor, just like our popular Flora. The board's also round and has alligator-clip pads around it so you don't have to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
  Neopixel Strip -- White (60/m): Neopixel Strip, White, 60 pixels per meter.
